# Fritzing sketch Blinds (saved by Fritzing 1.0.0rc)
breadboards: 1

parts:
  U1 = ESP32-38PinWide [part_number=ESP32-38PinWide]
  R1 = PHOTOCELL [package=photocell-kit]
  R2 = Resistor [tolerance=±5% power=0.25W resistance=220 package=THT]
  Driver1 = 28BYJ-48 Driver Module [part_number=ULN2003 package=THT]
  SM1 = 28BYJ-48 Stepper Motor [part_number=28BYJ-48]
  VCC1 = Battery block 9V  # not connected

nets:
  N1: U1.3.3, R1.P$2
  N2: U1.GPIO36, R1.P$1, R2.Pin_1
  N3: U1.GPIO32, Driver1.IN1
  N4: U1.GPIO33, Driver1.IN2
  N5: U1.GPIO25, Driver1.IN3
  N6: U1.GPIO26, Driver1.IN4
  N7: U1.GND, R2.Pin_0
  N8: Driver1.blue-pin, SM1.blue-pin
  N9: Driver1.pink-pin, SM1.pink-pin
  N10: Driver1.yellow-pin, SM1.yellow-pin
  N11: Driver1.orange-pin, SM1.orange-pin
  N12: Driver1.red-pin, SM1.red-pin

custom parts:
  ESP32-38PinWide: Generic 38-Pin ESP32 with wide format (only access to one side of pins on a breadboard) based on Stephen Lilley's HiLetgo ESP-WROOM-32 ESP32 ESP-32S Development Board.
  28BYJ-48 Driver Module: ULN2003 Driver Module for the 28BYJ-48 Unipolar Stepper Motor LED A - Blue wire - Bottom coil left LED B - Pink wire - Top coil left LED C - Yellow wire - Bottom coil right LED D - Orange wire - Top coil right Common rail - red Connector pins: blue - pink - yellow - orange - red Control pins - IN1 to IN4 Power pins - GND & Vmotor (5-12V) On/Off jumper (if removed, power to motor is cut).
  28BYJ-48 Stepper Motor: Unipolar Stepper Motor 28BYJ-48 Top coil - pink & orange Bottom coil - blue & yellow Common rail - red Connector pins: blue - pink - yellow - orange - red
